// Logisim project MiniPC.circ as structural Verilog: 6 circuits, main circuit main
module main (
);

  wire [7:0] alu_1_output, rom_1_data;

  ROM rom_1 (.data(rom_1_data));  // open: addr, sel
  Clock clock_1 ();  // open: out
  Register_Bank register_bank_1 ();  // open: Input, Read_1, Read_2, Write, clock, Output_1, Output_2, Instruction_Pointer
  // Probe on alu_1_output
  ALU alu_1 (.Output(alu_1_output));  // open: input_1, Input_2, Instruction

  // Notes on the sheet:
  //   contents of rom_1 (hex, n*v repeats v):
  //   80
endmodule

module ALU (
  input  [7:0] input_1,
  input  [7:0] Input_2,
  input  [1:0] Instruction,
  output [7:0] Output
);

  wire [2:0] undriven;

  _8bit_Adder u_8bit_adder_1 ();  // open: Input_1, Input_2, Output, C_in, C_out
  // XOR_Gate xor_1 is placed but not wired
  // NOT_Gate not_1 is placed but not wired
  Shifter #(.shift("ar")) shifter_1 (.\dist (undriven));  // open: in, out
  Multiplexer #(.select(2), .width(8)) multiplexer_1 ();  // open: in0, in1, in2, in3, out, sel, en
endmodule

module Register (
  input  clock,
  input  Write,
  input  [7:0] Input,
  output [7:0] \output 
);

  wire undriven;

  D_Flip_Flop d_ff_1 (.clk(Input[0]), .D(undriven), .Q(\output [0]));  // open: Qn, preset, en, reset
  D_Flip_Flop d_ff_2 (.D(undriven));  // open: clk, Q, Qn, preset, en, reset
  D_Flip_Flop d_ff_3 ();  // open: clk, D, Q, Qn, preset, en, reset
  D_Flip_Flop d_ff_4 ();  // open: clk, D, Q, Qn, preset, en, reset
  D_Flip_Flop d_ff_5 ();  // open: clk, D, Q, Qn, preset, en, reset
endmodule

module Register_Bank (
  input  clock,
  input  [7:0] Input,
  input  [1:0] Write,
  input  [1:0] Read_1,
  input  [1:0] Read_2,
  output [7:0] Output_1,
  output [7:0] Output_2,
  output [7:0] Instruction_Pointer
);

  Demultiplexer #(.select(2), .width(8)) demultiplexer_1 ();  // open: out0, out1, out2, out3, in, sel, en
  Decoder #(.select(2)) decoder_1 ();  // open: out0, out1, out2, out3, sel, en
  Multiplexer #(.width(8)) multiplexer_1 ();  // open: in0, in1, out, sel, en
  Register_part register_1 ();  // open: D, en, Q, clk, clr
  Register_part register_2 ();  // open: D, en, Q, clk, clr
  Register_part register_3 ();  // open: D, en, Q, clk, clr
  Register_part register_4 ();  // open: D, en, Q, clk, clr
  // _8bit_Adder 8bit_adder_1: pin names not known; wires that end beside it: {8{1'b0}}, 1'b1
  Multiplexer #(.select(2), .width(8)) multiplexer_2 ();  // open: in0, in1, in2, in3, out, sel, en
  Multiplexer #(.select(2), .width(8)) multiplexer_3 ();  // open: in0, in1, in2, in3, out, sel, en
endmodule

module Adder (
  input  C_in,
  input  Input_1,
  input  Input_2,
  output Output,
  output C_out
);
endmodule

module _8bit_Adder (
  input  [7:0] Input_1,
  input  [7:0] Input_2,
  input  C_in,
  output [7:0] Output,
  output C_out
);

  wire adder_1_c_out, adder_2_c_out, adder_3_c_out, adder_4_c_out, adder_5_c_out, adder_6_c_out,
       adder_7_c_out;

  Adder adder_1 (.C_in(C_in), .Input_1(Input_2[0]), .Input_2(Input_1[0]), .Output(Output[0]), .C_out(adder_1_c_out));
  Adder adder_2 (
    .C_in(adder_1_c_out), .Input_1(Input_2[1]), .Input_2(Input_1[1]), .Output(Output[1]),
    .C_out(adder_2_c_out));
  Adder adder_3 (
    .C_in(adder_2_c_out), .Input_1(Input_2[2]), .Input_2(Input_1[2]), .Output(Output[2]),
    .C_out(adder_3_c_out));
  Adder adder_4 (
    .C_in(adder_3_c_out), .Input_1(Input_2[3]), .Input_2(Input_1[3]), .Output(Output[3]),
    .C_out(adder_4_c_out));
  Adder adder_5 (
    .C_in(adder_4_c_out), .Input_1(Input_2[4]), .Input_2(Input_1[4]), .Output(Output[4]),
    .C_out(adder_5_c_out));
  Adder adder_6 (
    .C_in(adder_5_c_out), .Input_1(Input_2[5]), .Input_2(Input_1[5]), .Output(Output[5]),
    .C_out(adder_6_c_out));
  Adder adder_7 (
    .C_in(adder_6_c_out), .Input_1(Input_2[6]), .Input_2(Input_1[6]), .Output(Output[6]),
    .C_out(adder_7_c_out));
  Adder adder_8 (.C_in(adder_7_c_out), .Input_1(Input_2[7]), .Input_2(Input_1[7]), .Output(Output[7]), .C_out(C_out));
endmodule
