// Logisim project MiniPc_Sol.circ as structural Verilog: 6 circuits, main circuit main
module main (
);

  wire clock_1_out;
  wire [7:0] alu_1_output, register_bank_1_instruction_pointer, register_bank_1_output_1,
       register_bank_1_output_2, rom_1_data;

  ROM rom_1 (.addr(register_bank_1_instruction_pointer), .data(rom_1_data));  // open: sel
  Clock clock_1 (.out(clock_1_out));
  Register_Bank register_bank_1 (
    .Input(alu_1_output), .Read_1(rom_1_data[1:0]), .Read_2(rom_1_data[3:2]), .Write(rom_1_data[5:4]),
    .clock(clock_1_out), .Output_1(register_bank_1_output_1), .Output_2(register_bank_1_output_2),
    .Instruction_Pointer(register_bank_1_instruction_pointer));
  // Probe on alu_1_output
  ALU alu_1 (
    .input_1(register_bank_1_output_1), .Input_2(register_bank_1_output_2), .Instruction(rom_1_data[7:6]),
    .Output(alu_1_output));

  // Notes on the sheet:
  //   contents of rom_1 (hex, n*v repeats v):
  //   80
endmodule

module ALU (
  input  [7:0] input_1,
  input  [7:0] Input_2,
  input  [1:0] Instruction,
  output [7:0] Output
);

  wire [7:0] n8bit_adder_1_output, not_1_out, shifter_1_out, xor_1_out;

  _8bit_Adder u_8bit_adder_1 (
    .Input_1(input_1), .Input_2(Input_2), .Output(n8bit_adder_1_output), .C_in(1'b0));  // open: C_out
  assign xor_1_out = input_1 ^ Input_2;  // XOR_Gate xor_1, 8 bits wide
  assign not_1_out = ~input_1;  // NOT_Gate not_1, 8 bits wide
  Shifter #(.shift("ar")) shifter_1 (.in(input_1), .\dist (Input_2[2:0]), .out(shifter_1_out));
  Multiplexer #(.select(2), .width(8)) multiplexer_1 (
    .in0(n8bit_adder_1_output), .in1(xor_1_out), .in2(not_1_out), .in3(shifter_1_out), .out(Output),
    .sel(Instruction));  // open: en
endmodule

module Register (
  input  clock,
  input  Write,
  input  [7:0] Input,
  output [7:0] \output 
);

  wire undriven;

  D_Flip_Flop d_ff_1 (.clk(Input[0]), .D(undriven), .Q(\output [0]));  // open: Qn, preset, en, reset
  D_Flip_Flop d_ff_2 (.D(undriven));  // open: clk, Q, Qn, preset, en, reset
  D_Flip_Flop d_ff_3 ();  // open: clk, D, Q, Qn, preset, en, reset
  D_Flip_Flop d_ff_4 ();  // open: clk, D, Q, Qn, preset, en, reset
  D_Flip_Flop d_ff_5 ();  // open: clk, D, Q, Qn, preset, en, reset
endmodule

module Register_Bank (
  input  clock,
  input  [7:0] Input,
  input  [1:0] Write,
  input  [1:0] Read_1,
  input  [1:0] Read_2,
  output [7:0] Output_1,
  output [7:0] Output_2,
  output [7:0] Instruction_Pointer
);

  wire decoder_1_out0, decoder_1_out1, decoder_1_out2, decoder_1_out3;
  wire [7:0] demultiplexer_1_out0, demultiplexer_1_out1, demultiplexer_1_out2, demultiplexer_1_out3,
       multiplexer_1_out, n8bit_adder_1_output, register_1_q, register_2_q, register_3_q;

  Demultiplexer #(.select(2), .width(8)) demultiplexer_1 (
    .out0(demultiplexer_1_out0), .out1(demultiplexer_1_out1), .out2(demultiplexer_1_out2),
    .out3(demultiplexer_1_out3), .in(Input), .sel(Write));  // open: en
  Decoder #(.select(2)) decoder_1 (
    .out0(decoder_1_out0), .out1(decoder_1_out1), .out2(decoder_1_out2), .out3(decoder_1_out3), .sel(Write));  // open: en
  Register_part register_1 (.D(demultiplexer_1_out0), .en(decoder_1_out0), .Q(register_1_q), .clk(clock));  // open: clr
  Register_part register_2 (.D(demultiplexer_1_out1), .en(decoder_1_out1), .Q(register_2_q), .clk(clock));  // open: clr
  Register_part register_3 (.D(demultiplexer_1_out2), .en(decoder_1_out2), .Q(register_3_q), .clk(clock));  // open: clr
  Register_part register_4 (.D(multiplexer_1_out), .en(1'b1), .Q(Instruction_Pointer), .clk(clock));  // open: clr
  Multiplexer #(.width(8)) multiplexer_1 (
    .in0(n8bit_adder_1_output), .in1(demultiplexer_1_out3), .out(multiplexer_1_out), .sel(decoder_1_out3));  // open: en
  _8bit_Adder u_8bit_adder_1 (
    .Input_1(Instruction_Pointer), .Input_2({8{1'b0}}), .Output(n8bit_adder_1_output), .C_in(1'b1));  // open: C_out
  Multiplexer #(.select(2), .width(8)) multiplexer_2 (
    .in0(register_1_q), .in1(register_2_q), .in2(register_3_q), .in3(Instruction_Pointer), .out(Output_1),
    .sel(Read_1));  // open: en
  Multiplexer #(.select(2), .width(8)) multiplexer_3 (
    .in0(register_1_q), .in1(register_2_q), .in2(register_3_q), .in3(Instruction_Pointer), .out(Output_2),
    .sel(Read_2));  // open: en
endmodule

module Adder (
  input  C_in,
  input  Input_1,
  input  Input_2,
  output Output,
  output C_out
);

  wire and_1_out, and_2_out, xor_1_out;

  xor xor_1 (xor_1_out, Input_1, Input_2);
  and and_1 (and_1_out, Input_1, Input_2);
  xor xor_2 (Output, C_in, xor_1_out);
  and and_2 (and_2_out, xor_1_out, C_in);
  or or_1 (C_out, and_2_out, and_1_out);
endmodule

module _8bit_Adder (
  input  [7:0] Input_1,
  input  [7:0] Input_2,
  input  C_in,
  output [7:0] Output,
  output C_out
);

  wire adder_1_c_out, adder_2_c_out, adder_3_c_out, adder_4_c_out, adder_5_c_out, adder_6_c_out,
       adder_7_c_out;

  Adder adder_1 (.C_in(C_in), .Input_1(Input_2[0]), .Input_2(Input_1[0]), .Output(Output[0]), .C_out(adder_1_c_out));
  Adder adder_2 (
    .C_in(adder_1_c_out), .Input_1(Input_2[1]), .Input_2(Input_1[1]), .Output(Output[1]),
    .C_out(adder_2_c_out));
  Adder adder_3 (
    .C_in(adder_2_c_out), .Input_1(Input_2[2]), .Input_2(Input_1[2]), .Output(Output[2]),
    .C_out(adder_3_c_out));
  Adder adder_4 (
    .C_in(adder_3_c_out), .Input_1(Input_2[3]), .Input_2(Input_1[3]), .Output(Output[3]),
    .C_out(adder_4_c_out));
  Adder adder_5 (
    .C_in(adder_4_c_out), .Input_1(Input_2[4]), .Input_2(Input_1[4]), .Output(Output[4]),
    .C_out(adder_5_c_out));
  Adder adder_6 (
    .C_in(adder_5_c_out), .Input_1(Input_2[5]), .Input_2(Input_1[5]), .Output(Output[5]),
    .C_out(adder_6_c_out));
  Adder adder_7 (
    .C_in(adder_6_c_out), .Input_1(Input_2[6]), .Input_2(Input_1[6]), .Output(Output[6]),
    .C_out(adder_7_c_out));
  Adder adder_8 (.C_in(adder_7_c_out), .Input_1(Input_2[7]), .Input_2(Input_1[7]), .Output(Output[7]), .C_out(C_out));
endmodule
